// Digital circuit Memory Controller.dig as structural Verilog
module Memory_Controller (
  input  U_Program,
  input  CTR_CLK,
  input  CTR_MI,
  input  U_Write,
  input  U_Inspect,
  input  CTR_HLT,
  input  CTR_RI,
  input  CTR_RO,
  output RAM_CE,
  output RAM_WE,
  output RAM_OE,
  output U_OE,
  output Bus_OE,
  output Bus_Dir,
  output Halt_Out,
  output MAR_Cp
);

  wire and_1_out, and_2_out, and_3_out, and_4_out, and_5_out, and_6_out, and_7_out, and_8_out, and_9_out,
       and_10_out, and_11_out, not_1_out, not_2_out, not_3_out, not_4_out, not_5_out;

  not not_1 (not_1_out, U_Program);
  not not_2 (not_2_out, U_Write);
  not not_3 (not_3_out, U_Inspect);
  not not_4 (not_4_out, CTR_RI);
  not not_5 (not_5_out, CTR_RO);
  and and_1 (and_1_out, not_4_out, not_5_out, not_1_out);
  and and_2 (and_2_out, CTR_RI, CTR_RO, not_1_out);
  and and_3 (and_3_out, not_4_out, not_1_out);
  and and_4 (and_4_out, CTR_RO, not_1_out);
  and and_5 (and_5_out, U_Inspect, U_Program);
  and and_6 (and_6_out, U_Program, not_2_out);
  and and_7 (and_7_out, CTR_RI, not_1_out);
  and and_8 (and_8_out, not_5_out, not_1_out);
  and and_9 (and_9_out, not_3_out, U_Program);
  or or_1 (U_OE, U_Inspect, not_1_out);
  and and_10 (and_10_out, not_4_out, not_5_out);
  and and_11 (and_11_out, CTR_RI, CTR_RO);
  and and_12 (Bus_Dir, CTR_RI, not_5_out, not_1_out);
  or or_2 (Halt_Out, CTR_HLT, U_Program);
  and and_13 (MAR_Cp, CTR_CLK, CTR_MI);
  or or_3 (RAM_CE, and_1_out, and_2_out);
  or or_4 (RAM_OE, and_7_out, and_8_out, and_9_out);
  or or_5 (Bus_OE, and_10_out, and_11_out, U_Program);
  or or_6 (RAM_WE, and_3_out, and_4_out, and_5_out, and_6_out);
endmodule
